// Logisim project control_logic.circ as structural Verilog: 5 circuits, main circuit control_logic
module control_logic (
  input  [31:0] inst,
  input  BrEq,
  input  BrLt,
  output PCSel,
  output RegWEn,
  output [2:0] ImmSel,
  output BrUn,
  output ASel,
  output BSel,
  output [3:0] ALUSel,
  output MemRW,
  output [1:0] WBSel
);

  wire comparator_1_eq, comparator_2_eq, comparator_3_eq, comparator_4_eq, comparator_5_eq, comparator_6_eq,
       comparator_7_eq, comparator_8_eq, comparator_9_eq, comparator_10_eq, comparator_11_eq,
       comparator_12_eq, comparator_13_eq, comparator_14_eq, comparator_15_eq, or_1_out, or_4_out, or_5_out;
  wire [6:0] opcode;

  // Probe on opcode
  Comparator #(.width(7)) comparator_1 (.a(opcode), .b(7'b0010011), .eq(comparator_1_eq));  // open: gt, lt
  // Probe on 7'b0010011
  Comparator #(.width(7)) comparator_2 (.a(opcode), .b(7'b0000011), .eq(comparator_2_eq));  // open: gt, lt
  // Probe on 7'b0000011
  // Probe on 7'b0010001
  // Probe on 7'b1100011
  // Probe on 7'b0110111
  // Probe on 7'b1101111
  // Probe on 7'b0010011
  assign ImmSel = or_1_out ? 3'b000 : 3'bz;  // Controlled_Buffer controlled_buffer_1
  or or_1 (or_1_out, comparator_1_eq, comparator_2_eq);
  assign ImmSel = comparator_3_eq ? 3'b001 : 3'bz;  // Controlled_Buffer controlled_buffer_2
  Comparator #(.width(7)) comparator_3 (.a(opcode), .b(7'b0010001), .eq(comparator_3_eq));  // open: gt, lt
  assign ImmSel = comparator_4_eq ? 3'b010 : 3'bz;  // Controlled_Buffer controlled_buffer_3
  Comparator #(.width(7)) comparator_4 (.a(opcode), .b(7'b1100011), .eq(comparator_4_eq));  // open: gt, lt
  assign ImmSel = comparator_5_eq ? 3'b011 : 3'bz;  // Controlled_Buffer controlled_buffer_4
  Comparator #(.width(7)) comparator_5 (.a(opcode), .b(7'b0110111), .eq(comparator_5_eq));  // open: gt, lt
  assign ImmSel = comparator_6_eq ? 3'b100 : 3'bz;  // Controlled_Buffer controlled_buffer_5
  Comparator #(.width(7)) comparator_6 (.a(opcode), .b(7'b1101111), .eq(comparator_6_eq));  // open: gt, lt
  // Probe on 7'b0110111
  // Probe on 7'b1101111
  // Probe on 7'b0110011
  getOpCode getopcode_1 (.in_1(inst), .out_2(opcode));
  // Probe on opcode
  Comparator #(.width(7)) comparator_7 (.a(opcode), .b(7'b0010011), .eq(comparator_7_eq));  // open: gt, lt
  Comparator #(.width(7)) comparator_8 (.a(opcode), .b(7'b0110111), .eq(comparator_8_eq));  // open: gt, lt
  Comparator #(.width(7)) comparator_9 (.a(opcode), .b(7'b1101111), .eq(comparator_9_eq));  // open: gt, lt
  Comparator #(.width(7)) comparator_10 (.a(opcode), .b(7'b0110011), .eq(comparator_10_eq));  // open: gt, lt
  not not_1 (BSel, comparator_10_eq);
  buf or_2 (RegWEn, comparator_7_eq);  // OR_Gate
  or or_3 (ASel, comparator_8_eq, comparator_9_eq);
  // Probe on BSel
  // Probe on RegWEn
  // Probe on ASel
  // Probe on 7'b0110011
  // Probe on 7'b0010011
  // Probe on 7'b0000011
  // Probe on 7'b0110111
  // Probe on 7'b1101111
  Comparator #(.width(7)) comparator_11 (.a(opcode), .b(7'b0110011), .eq(comparator_11_eq));  // open: gt, lt
  Comparator #(.width(7)) comparator_12 (.a(opcode), .b(7'b0010011), .eq(comparator_12_eq));  // open: gt, lt
  Comparator #(.width(7)) comparator_13 (.a(opcode), .b(7'b0000011), .eq(comparator_13_eq));  // open: gt, lt
  Comparator #(.width(7)) comparator_14 (.a(opcode), .b(7'b0110111), .eq(comparator_14_eq));  // open: gt, lt
  Comparator #(.width(7)) comparator_15 (.a(opcode), .b(7'b1101111), .eq(comparator_15_eq));  // open: gt, lt
  or or_4 (or_4_out, comparator_11_eq, comparator_12_eq, comparator_13_eq);
  or or_5 (or_5_out, comparator_14_eq, comparator_15_eq);
  // Probe on ALUSel
  makeALUSel makealusel_1 (.in_1(inst), .out_2(ALUSel));
  assign WBSel = or_4_out ? 2'b00 : 2'bz;  // Controlled_Buffer Selects_ALURes
  assign WBSel = or_5_out ? 2'b01 : 2'bz;  // Controlled_Buffer Selects_PC

  // Notes on the sheet:
  //   INPUTS to your circuit
  //   DON'T CHANGE THE LOCATIONS OF THE INPUTS AND OUTPUTS!
  //   OUTPUT from your circuit
endmodule

module getOpCode (
  input  [31:0] in_1,
  output [6:0] out_2
);

  // Probe on in_1[6:0]

  assign out_2 = in_1[6:0];
endmodule

module getFunc3 (
  input  [31:0] in_1,
  output [2:0] out_2
);


  assign out_2 = in_1[14:12];
endmodule

module getFunc7 (
  input  [31:0] in_1,
  output [6:0] out_2
);


  assign out_2 = in_1[31:25];
endmodule

module makeALUSel (
  input  [31:0] in_1,
  output [3:0] out_2
);

  wire and_1_out, and_2_out, and_3_out, and_4_out, comparator_1_eq, comparator_2_eq, comparator_3_eq,
       comparator_4_eq, comparator_5_eq, comparator_6_eq, comparator_7_eq, comparator_8_eq, comparator_9_eq,
       comparator_10_eq, comparator_11_eq, comparator_12_eq, comparator_13_eq, comparator_14_eq,
       comparator_15_eq, or_1_out;
  wire [2:0] func3;
  wire [3:0] undriven;
  wire [6:0] func7, opcode;

  // Probe on opcode
  getOpCode getopcode_1 (.in_1(in_1), .out_2(opcode));
  getFunc3 getfunc3_1 (.in_1(in_1), .out_2(func3));
  // getFunc7 getfunc7_1: pin names not known; wires that end beside it: in_1, func7
  // Probe on opcode
  Comparator #(.width(7)) comparator_1 (.a(opcode), .b(7'b0110011), .eq(comparator_1_eq));  // open: gt, lt
  Comparator #(.width(3)) comparator_2 (.a(func3), .b(3'b000), .eq(comparator_2_eq));  // open: gt, lt
  Comparator #(.width(7)) comparator_3 (.a(opcode), .b(7'b0010011), .eq(comparator_3_eq));  // open: gt, lt
  Comparator #(.width(3)) comparator_4 (.a(func3), .b(3'b000), .eq(comparator_4_eq));  // open: gt, lt
  Comparator #(.width(3)) comparator_5 (.a(func3), .b(3'b001), .eq(comparator_5_eq));  // open: gt, lt
  Comparator #(.width(3)) comparator_6 (.a(func3), .b(3'b010), .eq(comparator_6_eq));  // open: gt, lt
  Comparator #(.width(3)) comparator_7 (.a(func3), .b(3'b011), .eq(comparator_7_eq));  // open: gt, lt
  Comparator #(.width(3)) comparator_8 (.a(func3), .b(3'b100), .eq(comparator_8_eq));  // open: gt, lt
  Comparator #(.width(3)) comparator_9 (.a(func3), .b(3'b101), .eq(comparator_9_eq));  // open: gt, lt
  Comparator #(.width(3)) comparator_10 (.a(func3), .b(3'b101), .eq(comparator_10_eq));  // open: gt, lt
  Comparator #(.width(3)) comparator_11 (.a(func3), .b(3'b110), .eq(comparator_11_eq));  // open: gt, lt
  Comparator #(.width(3)) comparator_12 (.a(func3), .b(3'b111), .eq(comparator_12_eq));  // open: gt, lt
  Comparator #(.width(7)) comparator_13 (.a(func7), .b({7{1'b0}}), .eq(comparator_13_eq));  // open: gt, lt
  Comparator #(.width(7)) comparator_14 (.b({7{1'b0}}), .eq(comparator_14_eq));  // open: a, gt, lt
  and and_1 (and_1_out, comparator_10_eq, comparator_15_eq);
  Comparator #(.width(7)) comparator_15 (.b(7'b0100000), .eq(comparator_15_eq));  // open: a, gt, lt
  and and_2 (and_2_out, comparator_1_eq, comparator_2_eq, comparator_13_eq);
  and and_3 (and_3_out, comparator_3_eq, comparator_4_eq);
  assign out_2 = comparator_5_eq ? 4'b0110 : 4'bz;  // Controlled_Buffer mysll
  assign out_2 = comparator_6_eq ? 4'b0111 : 4'bz;  // Controlled_Buffer myslt
  assign out_2 = comparator_7_eq ? undriven : 4'bz;  // Controlled_Buffer mysltu
  assign out_2 = comparator_8_eq ? 4'b0011 : 4'bz;  // Controlled_Buffer myxor
  assign out_2 = and_4_out ? 4'b0100 : 4'bz;  // Controlled_Buffer mysrl
  and and_4 (and_4_out, comparator_9_eq, comparator_14_eq);
  assign out_2 = and_1_out ? 4'b0101 : 4'bz;  // Controlled_Buffer mysra
  assign out_2 = comparator_11_eq ? 4'b0010 : 4'bz;  // Controlled_Buffer myor
  assign out_2 = comparator_12_eq ? 4'b0001 : 4'bz;  // Controlled_Buffer myand
  or or_1 (or_1_out, and_2_out, and_3_out);
  assign out_2 = or_1_out ? 4'b0000 : 4'bz;  // Controlled_Buffer add

  // Other names for the same wires on the sheet: ALUSel[3:0] = out_2
endmodule
