// Logisim project cpu.circ as structural Verilog: 1 circuit, main circuit main
module main (
  input  [31:0] INSTRUCTION,
  input  in_2,
  output [31:0] PROGRAM_COUNTER,
  output [31:0] ra,
  output [31:0] sp,
  output [31:0] t0,
  output [31:0] t1,
  output [31:0] t2,
  output [31:0] s0,
  output [31:0] s1,
  output [31:0] a0,
  output [31:0] out_12,
  output [31:0] out_13,
  output [31:0] out_14,
  output [3:0] out_15,
  output [31:0] out_16
);

  wire branch_comp_1_breq, branch_comp_1_brlt, clk, control_logic_1_asel, control_logic_1_brun,
       control_logic_1_bsel, control_logic_1_memrw, control_logic_1_regwen;
  wire [1:0] control_logic_1_wbsel;
  wire [2:0] control_logic_1_immsel;
  wire [31:0] A, adder_1_out, B, memRes, PROGRAM_COUNTER1, rs1Val, rs2Val, writeData;

  control_logic control_logic_1 (
    .BSel(control_logic_1_bsel), .BrUn(control_logic_1_brun), .RegWEn(control_logic_1_regwen),
    .ImmSel(control_logic_1_immsel), .ASel(control_logic_1_asel), .BrLt(branch_comp_1_brlt),
    .BrEq(branch_comp_1_breq), .inst(out_16), .ALUSel(out_15), .MemRW(control_logic_1_memrw),
    .WBSel(control_logic_1_wbsel));  // open: PCSel
  Clock clock_1 (.out(clk));
  Adder #(.width(32)) adder_1 (.a(PROGRAM_COUNTER), .b(32'h4), .out(adder_1_out));  // open: cin, cout
  Register #(.width(32)) PC (.D(adder_1_out), .clk(clk), .Q(PROGRAM_COUNTER));  // open: en, clr
  imm_gen imm_gen_1 (.ImmSel(control_logic_1_immsel), .inst(out_16), .imm(out_13));
  branch_comp branch_comp_1 (
    .BrEq(branch_comp_1_breq), .BrUn(control_logic_1_brun), .rs1(rs1Val), .BrLt(branch_comp_1_brlt),
    .rs2(rs2Val));
  Register #(.width(32)) register_1 (.D(INSTRUCTION), .en(1'b1), .clk(clk), .Q(out_16));  // open: clr
  Register #(.width(32)) register_2 (.D(PROGRAM_COUNTER), .en(1'b1), .clk(clk), .Q(PROGRAM_COUNTER1));  // open: clr
  // Probe on writeData
  // Probe on out_16[11:7]
  // Buffer buffer_1 is placed but not wired
  // Probe on control_logic_1_regwen
  regfile_main RegFile (
    .rs2(out_16[24:20]), .rd(out_16[11:7]), .Read_Data_1(rs1Val), .Read_Data_2(rs2Val), .ra(ra), .sp(sp),
    .t0(t0), .t1(t1), .t2(t2), .s0(s0), .s1(s1), .a0(a0), .rs1(out_16[19:15]), .Write_Data(writeData),
    .RegWEn(control_logic_1_regwen), .clk(clk));
  Multiplexer #(.width(32), .enable("false")) multiplexer_1 (
    .in0(rs1Val), .in1(PROGRAM_COUNTER1), .out(A), .sel(control_logic_1_asel));
  alu Arithmetic_Logic_Unit (.ALUSel(out_15), .Result(out_14), .A(A), .B(B));
  Multiplexer #(.width(32), .enable("false")) multiplexer_2 (
    .in0(rs2Val), .in1(out_13), .out(B), .sel(control_logic_1_bsel));
  // mem_main DMEM: pin names not known; wires that end beside it: control_logic_1_memrw, memRes
  Multiplexer #(.select(2), .width(32), .enable("false")) multiplexer_3 (
    .in0(out_14), .in1(memRes), .out(writeData), .sel(control_logic_1_wbsel));  // open: in2, in3

  assign out_12 = INSTRUCTION;

  // Other names for the same wires on the sheet: aluRes[31:0] = out_14; ALUSel[3:0] = out_15;
  //   Immediate[31:0] = out_13; INSTRUCTION1[31:0] = out_16; rd[4:0] = out_16[11:7]; rs1[4:0] = out_16[19:15];
  //   rs2[4:0] = out_16[24:20]

  // Notes on the sheet:
  //   Output
  //   IMEM (do **NOT** move this)
  //   Inputs
  //   It is OK to move the PC, RegFile, ALU, MEM, Branch Comp, Imm Gen, and Control Logic to wherever is most convenient for you when constructing your CPU, and to delete this text
  //   Inputs/Outputs for testing. Do **NOT** move these.
endmodule
