// Logisim project imm_gen.circ as structural Verilog: 3 circuits, main circuit imm_gen
module imm_gen (
  input  [31:0] inst,
  input  [2:0] ImmSel,
  output [31:0] imm
);

  wire comparator_1_eq, comparator_2_eq, comparator_3_eq, comparator_4_eq, comparator_5_eq;
  wire [31:0] sext1_1_out_2, sext1_2_out_2, sext1_3_out_2, sext2_1_out_2, sext2_2_out_2;

  SEXT1 sext1_1 (.in_1(inst[31:20]), .out_2(sext1_1_out_2));
  Comparator #(.width(3)) comparator_1 (.a(ImmSel), .b(3'b000), .eq(comparator_1_eq));  // open: gt, lt
  SEXT1 sext1_2 (.in_1({inst[31:25], inst[11:7]}), .out_2(sext1_2_out_2));
  Comparator #(.width(3)) comparator_2 (.a(ImmSel), .b(3'b001), .eq(comparator_2_eq));  // open: gt, lt
  SEXT1 sext1_3 (.in_1({inst[31], inst[7], inst[30:25], inst[11:8]}), .out_2(sext1_3_out_2));
  Comparator #(.width(3)) comparator_3 (.a(ImmSel), .b(3'b010), .eq(comparator_3_eq));  // open: gt, lt
  SEXT2 sext2_1 (.in_1(inst[31:12]), .out_2(sext2_1_out_2));
  Comparator #(.width(3)) comparator_4 (.a(ImmSel), .b(3'b011), .eq(comparator_4_eq));  // open: gt, lt
  SEXT2 sext2_2 (.in_1({inst[31], inst[19:12], inst[20], inst[30:21]}), .out_2(sext2_2_out_2));
  Comparator #(.width(3)) comparator_5 (.a(ImmSel), .b(3'b100), .eq(comparator_5_eq));  // open: gt, lt
  assign imm = comparator_1_eq ? sext1_1_out_2 : 32'bz;  // Controlled_Buffer controlled_buffer_1
  assign imm = comparator_2_eq ? sext1_2_out_2 : 32'bz;  // Controlled_Buffer controlled_buffer_2
  assign imm = comparator_3_eq ? sext1_3_out_2 : 32'bz;  // Controlled_Buffer controlled_buffer_3
  assign imm = comparator_4_eq ? sext2_1_out_2 : 32'bz;  // Controlled_Buffer controlled_buffer_4
  assign imm = comparator_5_eq ? sext2_2_out_2 : 32'bz;  // Controlled_Buffer controlled_buffer_5

  // Notes on the sheet:
  //   INPUTS to your circuit
  //   DON'T CHANGE THE LOCATIONS OF THE INPUTS AND OUTPUTS!
  //   OUTPUT from your circuit
endmodule

module SEXT1 (
  input  [11:0] in_1,
  output [31:0] out_2
);

  Multiplexer #(.width(20), .enable("false")) multiplexer_1 (
    .in0({20{1'b0}}), .in1({20{1'b1}}), .out(out_2[31:12]), .sel(in_1[11]));

  assign out_2[11:0] = in_1;
endmodule

module SEXT2 (
  input  [19:0] in_1,
  output [31:0] out_2
);

  Multiplexer #(.width(12), .enable("false")) multiplexer_1 (
    .in0({12{1'b0}}), .in1({12{1'b1}}), .out(out_2[31:20]), .sel(in_1[19]));

  assign out_2[19:0] = in_1;
endmodule
